# Fritzing sketch LCD-Print-Hello (saved by Fritzing 1.0.5)
breadboards: 1

parts:
  U1 = atmega328 [package=dip]
  LCD1 = LCD screen
  Power_plug1 = Power plug
  R1 = 12mm Trimmer Potentiometer (Large) [maximum_resistance=10kΩ knob_status=50% power=0.5W package=THT]

nets:
  N1: U1.D4, LCD1.DB4
  VCC: U1.VCC, LCD1.VDD, LCD1.LED+, Power_plug1.VCC, R1.leg2
  VSS: U1.GND#7, LCD1.VSS, LCD1.R/W, LCD1.LED-, Power_plug1.GND, R1.leg1
  N2: U1.D5_(PWM), LCD1.DB5
  N3: U1.D6_(PWM), LCD1.DB6
  N4: U1.D7, LCD1.DB7
  N5: U1.A0, LCD1.RS
  N6: U1.A1, LCD1.E
  N7: LCD1.V0, R1.wiper
